# Fritzing sketch Schema2 (saved by Fritzing 0.9.3b)
breadboards: 1

parts:
  V1 = DC Power [voltage=12V]
  U3 = Voltage Regulator - 5V [package="TO220 [THT]"]
  part = Tantalum Capacitor [capacitance=22µF voltage=6.3V package="100 mil [THT, tantalum]"]
  part_2 = Tantalum Capacitor [capacitance=0.1µF package="100 mil [THT, tantalum]"]
  D2 = Rectifier Diode [part_number=1N4001 package="Melf DO-213 AB [SMD]"]
  Elettrovalvola = DC Motor
  Q2 = NPN-Transistor [package="TO92 [THT]"]
  part_3 = Resistor [tolerance=±5% resistance=2.2k package=THT]
  A4989 = A4988 Stepper Motor Driver Carrier
  U4 = ESP32-38PinWide [part_number=ESP32-38PinWide]
  M1 = Stepper Motor - Bipolar
  Mod1 = KY-015 Temperature & Humidity Sensor Module [package="Breakout board"]
  Componente1 = FC-28 Soil Hygrometer Module - Probe
  부품3 = FC-28 Soil Hygrometer Module
  YL-83_-_Control_Board2 = YL-83 Rain Sensor - Control Board
  YL-83_-_Detection_Board2 = YL-83 Rain Sensor - Detection Board

nets:
  VCC: V1.V+, U3.input_voltage, part.+, D2.cathode, Elettrovalvola.pin_1, A4989.VMOT, 부품3.VCC, YL-83_-_Control_Board2.VCC
  GND: V1.V-, U3.GND, part.-, part_2.-, Q2.E, A4989.Enable, A4989.GROUND, U4.GND, Mod1.-, 부품3.GND, YL-83_-_Control_Board2.GND
  VIN: U3.output_voltage, part_2.+, D2.anode, A4989.RESET, A4989.SLEEP, A4989.VDD, U4.VIN, Mod1.Vin
  N1: Elettrovalvola.pin_2, Q2.C
  N2: Q2.B, part_3.Pin_0
  N3: part_3.Pin_1, U4.GPIO13
  N4: A4989.STEP, U4.GPIO17
  N5: A4989.DIR, U4.GPIO16
  N6: A4989.OUT_2B, M1.B
  N7: A4989.OUT_2A, M1.A
  N8: A4989.OUT_1A, M1.C
  N9: A4989.OUT_1B, M1.D
  N10: U4.GPIO34, 부품3.AO
  N11: U4.GPIO35, YL-83_-_Control_Board2.AO
  N12: U4.GPIO23, Mod1.S
  N13: Componente1.POS, 부품3.POS
  N14: Componente1.NEG, 부품3.NEG
  N15: YL-83_-_Control_Board2.POS, YL-83_-_Detection_Board2.POS
  N16: YL-83_-_Control_Board2.NEG, YL-83_-_Detection_Board2.NEG

custom parts:
  ESP32-38PinWide: Generic 38-Pin ESP32 with wide format (only access to one side of pins on a breadboard) based on Stephen Lilley's HiLetgo ESP-WROOM-32 ESP32 ESP-32S Development Board.
  KY-015 Temperature & Humidity Sensor Module: KY-015 temperature and humidity sensor module, provides a low-latency serial interface to measure humidity and temperature.
  FC-28 Soil Hygrometer Module - Probe: The FC-28 is a soil hygrometer module that uses the Texas Instruments LM393 comparator chip to provide an analog measurement of soil humidity.
  FC-28 Soil Hygrometer Module: The FC-28 is a soil hygrometer module that uses the Texas Instruments LM393 comparator chip to provide an analog measurement of soil humidity. The digital output is high when soil moisture is over a certain threshold, as determined by adjusting the potentiometer.
  YL-83 Rain Sensor - Control Board: The YL-83 is a rain sensor that has more resistance when dry and less resistance when wet. The module runs at 5V.
  YL-83 Rain Sensor - Detection Board: The YL-83 is a rain sensor that has more resistance when dry and less resistance when wet. The module runs at 5V.
